// Digital circuit addressSpace.dig as structural Verilog
module addressSpace (
  input  C,
  input  [15:0] Ia,
  input  [15:0] Da,
  input  [15:0] Din,
  input  str,
  output [15:0] I,
  output [15:0] D
);

  wire and_1_out;
  wire [15:0] Data_d, Program_d, RAM_d1, RAM_d2;

  and and_1 (and_1_out, str, Da[13]);
  ROM #(.AddrBits(13), .Bits(16)) Program (.A(Ia[12:0]), .sel(1'b1), .D(Program_d));
  ROM #(.AddrBits(13), .Bits(16)) Data (.A(Da[12:0]), .sel(1'b1), .D(Data_d));
  RAMDualAccess #(.AddrBits(13), .Bits(16)) RAM (
    .str(and_1_out), .C(C), .ld(1'b1), .A1(Da[12:0]), .Din1(Din), .A2(Ia[12:0]), .D1(RAM_d1), .D2(RAM_d2));
  Multiplexer #(.Bits(16)) multiplexer_1 (.sel(Ia[13]), .in_0(Program_d), .in_1(RAM_d2), .out(I));
  Multiplexer #(.Bits(16)) multiplexer_2 (.sel(Da[13]), .in_0(Data_d), .in_1(RAM_d1), .out(D));

  // Other names for the same wires on the sheet: Data_High = Da[13]; Inst_High = Ia[13]

  // Notes on the sheet:
  //   contents of Program (hex, n*v repeats v):
  //   21a5,5130,5122,7463,6,2000,108,37
endmodule
