// Digital circuit alu.dig as structural Verilog
module alu (
  input  [15:0] a,
  input  [15:0] b,
  input  [5:0] op,
  input  C,
  output [15:0] out
);

  wire and_1_out, and_3_out, xor_3_out;
  wire [0:0] add_2_c_o, not_1_out, not_2_out, not_3_out, Signed_eq, Signed_gt, Unsigned_gt;
  wire [15:0] add_2_s, and_2_out, bitextender_1_out, bitextender_2_out, \cᵢ__16 , or_1_out, or_2_out,
       \shiftleft_1_cₒ , shiftleft_1_out, \shiftright_1_cₒ , shiftright_1_out, xor_1_out, xor_2_out;
  wire [16:0] \cₒ , register_1_q;
  wire [16:16] add_1_c_o, \cᵢ__17 ;
  wire [31:0] add_1_s, mul_1_mul, mul_2_mul, multiplexer_2_out;

  and and_1 (and_1_out, ~op[3], ~op[2]);  // And
  Register #(.Bits(17)) register_1 (.D(\cₒ ), .C(C), .en(and_1_out), .Q(register_1_q));
  Multiplexer #(.Bits(17)) multiplexer_1 (
    .sel(op[5]), .in_0({17{1'b0}}), .in_1(register_1_q), .out({\cᵢ__17 [16], \cᵢ__16 }));
  Mul #(.Bits(16)) mul_1 (.a(a), .b(b), .mul(mul_1_mul));
  Mul #(.Signed("true"), .Bits(16)) mul_2 (.a(a), .b(b), .mul(mul_2_mul));
  Comparator #(.Bits(16), .Signed("true")) Signed (.a(a), .b(b), .gt(Signed_gt[0]), .eq(Signed_eq[0]));  // open: lt
  Comparator #(.Bits(16)) Unsigned (.a(a), .b(b), .gt(Unsigned_gt[0]));  // open: eq, lt
  Multiplexer #(.Bits(32)) multiplexer_2 (.sel(op[4]), .in_0(mul_1_mul), .in_1(mul_2_mul), .out(multiplexer_2_out));
  Add #(.Bits(32)) add_1 (
    .a(multiplexer_2_out), .b({{15{1'b0}}, \cᵢ__17 [16], \cᵢ__16 }), .c_i(1'b0), .s(add_1_s),
    .c_o(add_1_c_o[16]));
  not not_1 (not_1_out[0], Signed_eq[0]);
  not not_2 (not_2_out[0], Signed_gt[0]);
  not not_3 (not_3_out[0], Unsigned_gt[0]);
  assign or_1_out = a | b;  // Or or_1, 16 bits wide
  assign and_2_out = a & b;  // And and_2, 16 bits wide
  assign xor_1_out = a ^ b;  // XOr xor_1, 16 bits wide
  BitExtender #(.inputBits(1)) bitextender_1 (.in(op[4]), .out(bitextender_1_out));
  and and_3 (and_3_out, a[0], op[4]);
  assign xor_2_out = bitextender_1_out ^ a;  // XOr xor_2, 16 bits wide
  xor xor_3 (xor_3_out, \cᵢ__16 [0], op[4]);
  BitExtender #(.inputBits(1)) bitextender_2 (.in(and_3_out), .out(bitextender_2_out));
  assign or_2_out = bitextender_2_out | \cᵢ__16 ;  // Or or_2, 16 bits wide
  Add #(.Bits(16)) add_2 (.a(xor_2_out), .b(b), .c_i(xor_3_out), .s(add_2_s), .c_o(add_2_c_o[0]));
  shiftLeft shiftleft_1 (.in(a), .fill(or_2_out), .shift(b[3:0]), .out(shiftleft_1_out), .\cₒ (\shiftleft_1_cₒ ));
  shiftRight shiftright_1 (.in(a), .fill(or_2_out), .shift(b[3:0]), .out(shiftright_1_out), .\cₒ (\shiftright_1_cₒ ));
  Multiplexer #(.Bits(16), .Selector_Bits(4)) multiplexer_3 (
    .sel(op[3:0]), .in_0(add_2_s), .in_1(add_1_s[15:0]), .in_2(shiftleft_1_out), .in_3(shiftright_1_out),
    .in_4(or_1_out), .in_5(and_2_out), .in_6(xor_1_out), .in_7({16{1'b0}}),
    .in_8({{15{1'b0}}, Signed_eq[0]}), .in_9({{15{1'b0}}, not_1_out[0]}), .in_10({{15{1'b0}}, Signed_gt[0]}),
    .in_11({{15{1'b0}}, not_2_out[0]}), .in_12({{15{1'b0}}, Unsigned_gt[0]}),
    .in_13({{15{1'b0}}, not_3_out[0]}), .in_14({16{1'b0}}), .in_15({16{1'b0}}), .out(out));
  Multiplexer #(.Bits(17), .Selector_Bits(2)) multiplexer_4 (
    .sel(op[1:0]), .in_0({{16{1'b0}}, add_2_c_o[0]}), .in_1({add_1_c_o[16], add_1_s[31:16]}),
    .in_2({1'b0, \shiftleft_1_cₒ }), .in_3({1'b0, \shiftright_1_cₒ }), .out(\cₒ ));

  // Other names for the same wires on the sheet: cᵢ__17[15:0] = \cᵢ__16 ; fun4[3:0] = op[3:0]; sub = op[4]

  // Notes on the sheet:
  //   Input
  //   Comparison
  //   Multiplication
  //   Bitwise Logic
  //   Addition & Subtraction
  //   Shifting
endmodule
