// Digital circuit canis.dig as structural Verilog
module canis (
  input  CLK,
  input  PIN_13,
  output PIN_22,
  output PIN_24,
  output PIN_21,
  output PIN_18,
  output PIN_19,
  output PIN_20,
  output PIN_23,
  output PIN_15,
  output PIN_14,
  output PIN_17,
  output PIN_16
);

  wire and_1_out, and_2_out, and_3_out, comparator_1_out, decoder_1_alubs, decoder_1_hault, decoder_1_jmp,
       decoder_1_out, decoder_1_str, decoder_1_we, demultiplexer_1_out_0, demultiplexer_1_out_1,
       demultiplexer_1_out_2, demultiplexer_1_out_3, demultiplexer_1_out_4, demultiplexer_1_out_5,
       demultiplexer_1_out_6, demultiplexer_1_out_7, Hault_q, multiplexer_1_out, not_1_out;
  wire [1:0] decoder_1_aluas, decoder_1_dsrc;
  wire [2:0] decoder_1_cmpo, decoder_1_imm, decoder_1_ra, decoder_1_rb, decoder_1_rw;
  wire [3:0] decoder_1_aluo;
  wire [15:0] add_1_s, addressspace_1_d, addressspace_1_i, alu_1_out, multiplexer_2_out, multiplexer_3_out,
       multiplexer_4_out, multiplexer_5_out, multiplexer_6_out, PC_q, register_1_q, register_2_q,
       register_3_q, register_4_q, register_5_q, register_6_q, register_7_q, register_8_q, Registers_da,
       Registers_db;
  wire [15:3] decoder_1_imm_2;

  Multiplexer multiplexer_1 (.sel(PIN_13), .in_0(decoder_1_hault), .in_1(1'b0), .out(multiplexer_1_out));
  Register #(.generic("this.Bits=int(args.bits);")) Hault (.D(multiplexer_1_out), .C(CLK), .en(1'b1), .Q(Hault_q));
  not not_1 (not_1_out, Hault_q);
  Register #(.Bits(16), .generic("this.Bits=int(args.bits);")) PC (
    .D(multiplexer_2_out), .C(CLK), .en(not_1_out), .Q(PC_q));
  Add #(.Bits(16)) add_1 (.a(PC_q), .b(16'h1), .c_i(1'b0), .s(add_1_s));  // open: c_o
  comparator comparator_1 (.val(Registers_da), .op(decoder_1_cmpo), .out(comparator_1_out));
  and and_1 (and_1_out, comparator_1_out, decoder_1_jmp);
  Multiplexer #(.Bits(16)) multiplexer_2 (.sel(and_1_out), .in_0(add_1_s), .in_1(alu_1_out), .out(multiplexer_2_out));
  and and_2 (and_2_out, decoder_1_str, not_1_out);
  addressSpace addressspace_1 (
    .C(CLK), .Ia(PC_q), .Da(alu_1_out), .Din(Registers_db), .str(and_2_out), .I(addressspace_1_i),
    .D(addressspace_1_d));
  decoder decoder_1 (
    .C(CLK), .I(addressspace_1_i), .imm({decoder_1_imm_2, decoder_1_imm}), .ALUaS(decoder_1_aluas),
    .ALUbS(decoder_1_alubs), .ALUo(decoder_1_aluo), .Dsrc(decoder_1_dsrc), .we(decoder_1_we),
    .Rw(decoder_1_rw), .Ra(decoder_1_ra), .Rb(decoder_1_rb), .str(decoder_1_str), .jmp(decoder_1_jmp),
    .CmpO(decoder_1_cmpo), .out(decoder_1_out), .hault(decoder_1_hault));
  Multiplexer #(.Selector_Bits(3), .Bits(16)) multiplexer_3 (
    .sel(decoder_1_imm), .in_0({16{1'b0}}), .in_1({16{1'b0}}), .in_2({16{1'b0}}), .in_3({16{1'b0}}),
    .in_4({16{1'b0}}), .in_5({16{1'b0}}), .in_6({16{1'b0}}), .in_7({16{1'b0}}), .out(multiplexer_3_out));
  Demultiplexer #(.Selector_Bits(3)) demultiplexer_1 (
    .sel(decoder_1_imm), .in(decoder_1_out), .out_0(demultiplexer_1_out_0), .out_1(demultiplexer_1_out_1),
    .out_2(demultiplexer_1_out_2), .out_3(demultiplexer_1_out_3), .out_4(demultiplexer_1_out_4),
    .out_5(demultiplexer_1_out_5), .out_6(demultiplexer_1_out_6), .out_7(demultiplexer_1_out_7));
  Multiplexer #(.Selector_Bits(2), .Bits(16)) multiplexer_4 (
    .sel(decoder_1_dsrc), .in_0(alu_1_out), .in_1(addressspace_1_d), .in_2(add_1_s),
    .in_3(multiplexer_3_out), .out(multiplexer_4_out));
  and and_3 (and_3_out, decoder_1_we, not_1_out);
  RegisterFile #(.AddrBits(3), .Bits(16)) Registers (
    .Din(multiplexer_4_out), .we(and_3_out), .Rw(decoder_1_rw), .C(CLK), .Ra(decoder_1_ra),
    .Rb(decoder_1_rb), .Da(Registers_da), .Db(Registers_db));
  Register #(.Bits(16)) register_1 (.D(Registers_da), .C(CLK), .en(demultiplexer_1_out_0), .Q(register_1_q));
  Register #(.Bits(16)) register_2 (.D(Registers_da), .C(CLK), .en(demultiplexer_1_out_1), .Q(register_2_q));
  Register #(.Bits(16)) register_3 (.D(Registers_da), .C(CLK), .en(demultiplexer_1_out_2), .Q(register_3_q));
  Register #(.Bits(16)) register_4 (.D(Registers_da), .C(CLK), .en(demultiplexer_1_out_3), .Q(register_4_q));
  Register #(.Bits(16)) register_5 (.D(Registers_da), .C(CLK), .en(demultiplexer_1_out_4), .Q(register_5_q));
  Register #(.Bits(16)) register_6 (.D(Registers_da), .C(CLK), .en(demultiplexer_1_out_5), .Q(register_6_q));
  Register #(.Bits(16)) register_7 (.D(Registers_da), .C(CLK), .en(demultiplexer_1_out_6), .Q(register_7_q));
  Register #(.Bits(16)) register_8 (.D(Registers_da), .C(CLK), .en(demultiplexer_1_out_7), .Q(register_8_q));
  Multiplexer #(.Selector_Bits(2), .Bits(16)) multiplexer_5 (
    .sel(decoder_1_aluas), .in_0(Registers_da), .in_1(add_1_s), .in_2({16{1'b0}}), .in_3({16{1'b0}}),
    .out(multiplexer_5_out));
  Multiplexer #(.Bits(16)) multiplexer_6 (
    .sel(decoder_1_alubs), .in_0(Registers_db), .in_1({decoder_1_imm_2, decoder_1_imm}),
    .out(multiplexer_6_out));
  hexDisplayDriver hexdisplaydriver_1 (
    .Cl(CLK), .num(register_1_q), .a(PIN_22), .b(PIN_24), .c(PIN_21), .d(PIN_18), .e(PIN_19), .f(PIN_20),
    .g(PIN_23), .W(PIN_15), .X(PIN_14), .Y(PIN_17), .Z(PIN_16));
  alu alu_1 (
    .C(CLK), .a(multiplexer_5_out), .b(multiplexer_6_out), .op(decoder_1_aluo), .en(not_1_out),
    .out(alu_1_out));
endmodule
