// Digital circuit comparator.dig as structural Verilog
module comparator (
  input  [15:0] val,
  input  [2:0] op,
  output out
);

  wire and_1_out, and_2_out, and_3_out, nor_1_out, nor_2_out;

  nor nor_1 (nor_1_out, val[0], val[1], val[2], val[3], val[4], val[5], val[6], val[7], val[9], val[10], val[11], val[12], val[13], val[14], val[15], val[8]);
  nor nor_2 (nor_2_out, val[15], nor_1_out);
  and and_1 (and_1_out, nor_2_out, op[2]);
  and and_2 (and_2_out, nor_1_out, op[1]);
  and and_3 (and_3_out, val[15], op[0]);
  or or_1 (out, and_1_out, and_2_out, and_3_out);

  // Notes on the sheet:
  //   Greater Than
  //   Equal
  //   Less than
endmodule
