// Digital circuit dwordToUnalignedBytes.dig as structural Verilog
module dwordToUnalignedBytes (
  input  [1:0] off,
  input  [31:0] D,
  output [7:0] b4,
  output [7:0] b3,
  output [7:0] b2,
  output [7:0] b1
);

  Multiplexer #(.Selector_Bits(2), .Bits(32)) multiplexer_1 (
    .sel(off), .in_0(D), .in_1({D[7:0], D[31:8]}), .in_2({D[15:0], D[31:16]}), .in_3({D[23:0], D[31:24]}),
    .out({b4, b3, b2, b1}));

  // Notes on the sheet:
  //   off: Byte offset
endmodule
