// Digital circuit eTypeBuffer.dig as structural Verilog
module eTypeBuffer (
  input  [15:0] I,
  input  C,
  output [31:0] Iext
);

  wire and_1_out, ExtendedLUT_d, IsExtended_nq, IsExtended_q;
  wire [15:0] LowerWord_q, multiplexer_1_out;

  Register #(.Bits(16), .generic("this.Bits=int(args.bits);")) LowerWord (
    .D(I), .C(C), .en(and_1_out), .Q(LowerWord_q));
  D_FF IsExtended (.D(and_1_out), .C(C), .Q(IsExtended_q), .nQ(IsExtended_nq));
  Multiplexer #(.Bits(16)) multiplexer_1 (.sel(IsExtended_q), .in_0(I), .in_1(LowerWord_q), .out(multiplexer_1_out));
  ROM #(.AddrBits(4)) ExtendedLUT (.A(multiplexer_1_out[3:0]), .sel(1'b1), .D(ExtendedLUT_d));
  and and_1 (and_1_out, ExtendedLUT_d, IsExtended_nq);
  Multiplexer #(.Bits(16)) multiplexer_2 (
    .sel(and_1_out), .in_0(multiplexer_1_out), .in_1({16{1'b0}}), .out(Iext[15:0]));

  assign Iext[31:16] = I;

  // Notes on the sheet:
  //   contents of ExtendedLUT (hex, n*v repeats v):
  //   4*0,1,0,1,6*0,1
endmodule
