// Digital circuit genericSplit16.dig as structural Verilog
module genericSplit16 (
  input  [15:0] \lsbᵢ ,
  input  [15:0] \msbᵢ ,
  output [15:0] out,
  output [15:0] \lsbₒ ,
  output [15:0] \msbₒ 
);


  assign \lsbₒ  = {\lsbᵢ [14:0], 1'b0};
  assign \msbₒ  = {{15{1'b0}}, \msbᵢ [15]};
  assign out = {\msbᵢ [14:0], \lsbᵢ [15]};
endmodule

/* Code that sets the parameters or builds the circuit:
split := 1;
*/
