// Digital circuit hexDisplayDriver.dig as structural Verilog
module hexDisplayDriver (
  input  Cl,
  input  [15:0] num,
  output a,
  output b,
  output c,
  output d,
  output e,
  output f,
  output g,
  output W,
  output X,
  output Y,
  output Z
);

  wire nand_1_out;
  wire [3:0] multiplexer_1_out;
  wire [5:0] counter_1_out;

  Counter #(.Bits(6)) counter_1 (.en(1'b1), .C(Cl), .clr(1'b0), .out(counter_1_out));  // open: ovf
  nand nand_1 (nand_1_out, counter_1_out[1], counter_1_out[3]);
  Multiplexer #(.Selector_Bits(2), .Bits(4)) multiplexer_1 (
    .sel(counter_1_out[5:4]), .in_0(num[3:0]), .in_1(num[7:4]), .in_2(num[11:8]), .in_3(num[15:12]),
    .out(multiplexer_1_out));
  ROM #(.AddrBits(4), .Bits(7)) Digits (.A(multiplexer_1_out), .sel(1'b1), .D({g, f, e, d, c, b, a}));
  Demultiplexer #(.Selector_Bits(2)) demultiplexer_1 (
    .sel(counter_1_out[5:4]), .in(nand_1_out), .out_0(W), .out_1(X), .out_2(Y), .out_3(Z));

  // Notes on the sheet:
  //   contents of Digits (hex, n*v repeats v):
  //   40,79,24,30,19,12,2,58,0,10,8,3,27,21,6,e
endmodule
