// Digital circuit interstageRegister.dig as structural Verilog
module interstageRegister (
  input  C,
  input  [15:0] D,
  input  pass,
  output [15:0] Q
);

  wire register_1_q;

  Register #(.generic("this.Bits=int(args.bits);")) register_1 (.D(D), .C(C), .en(pass), .Q(register_1_q));
  Multiplexer multiplexer_1 (.sel(pass), .in_0(1'b0), .in_1(register_1_q), .out(Q[0]));
  // Pins of 1 and 16 bits meet at Q
endmodule
