// Digital circuit memoryAccessTrimmer.dig as structural Verilog
module memoryAccessTrimmer (
  input  sign,
  input  [1:0] am,
  input  [31:0] Din,
  output [31:0] D
);

  wire [31:0] bitextender_1_out, bitextender_2_out, bitextender_3_out, multiplexer_1_out, multiplexer_2_out,
       multiplexer_3_out;

  BitExtender #(.inputBits(24), .outputBits(32)) bitextender_1 (.in(Din[23:0]), .out(bitextender_1_out));
  BitExtender #(.inputBits(16), .outputBits(32)) bitextender_2 (.in(Din[15:0]), .out(bitextender_2_out));
  BitExtender #(.outputBits(32)) bitextender_3 (.in(Din[7:0]), .out(bitextender_3_out));
  Multiplexer #(.Bits(32)) multiplexer_1 (
    .sel(sign), .in_0({{8{1'b0}}, Din[23:0]}), .in_1(bitextender_1_out), .out(multiplexer_1_out));
  Multiplexer #(.Bits(32)) multiplexer_2 (
    .sel(sign), .in_0({{16{1'b0}}, Din[15:0]}), .in_1(bitextender_2_out), .out(multiplexer_2_out));
  Multiplexer #(.Bits(32)) multiplexer_3 (
    .sel(sign), .in_0({{24{1'b0}}, Din[7:0]}), .in_1(bitextender_3_out), .out(multiplexer_3_out));
  Multiplexer #(.Selector_Bits(2), .Bits(32)) multiplexer_4 (
    .sel(am), .in_0(Din), .in_1(multiplexer_1_out), .in_2(multiplexer_2_out), .in_3(multiplexer_3_out),
    .out(D));
endmodule
