// Digital circuit memoryWriteControl.dig as structural Verilog
module memoryWriteControl (
  input  [1:0] off,
  input  we,
  input  [1:0] am,
  output we4,
  output we3,
  output we2,
  output we1
);

  wire [3:0] multiplexer_1_out, multiplexer_2_out;

  Multiplexer #(.Selector_Bits(2), .Bits(4)) multiplexer_1 (
    .sel(am), .in_0(4'b1111), .in_1(4'b0111), .in_2(4'b0011), .in_3(4'b0001), .out(multiplexer_1_out));
  Multiplexer #(.Selector_Bits(2), .Bits(4)) multiplexer_2 (
    .sel(off), .in_0(multiplexer_1_out), .in_1({multiplexer_1_out[0], multiplexer_1_out[3:1]}),
    .in_2({multiplexer_1_out[1:0], multiplexer_1_out[3:2]}),
    .in_3({multiplexer_1_out[2:0], multiplexer_1_out[3]}), .out(multiplexer_2_out));
  Multiplexer #(.Bits(4)) multiplexer_3 (
    .sel(we), .in_0(4'b0000), .in_1(multiplexer_2_out), .out({we4, we3, we2, we1}));

  // Notes on the sheet:
  //   off: Byte offset
endmodule
