// Digital circuit ram.dig as structural Verilog
module ram (
  input  C,
  input  [15:0] _1A,
  input  [31:0] _1Din,
  input  [15:0] _2A,
  input  we,
  input  [1:0] am,
  input  sign,
  output [31:0] _1D,
  output [31:0] _2D
);

  wire and_1_out, and_2_out, memorywritecontrol_1_we1, memorywritecontrol_1_we2, memorywritecontrol_1_we3,
       memorywritecontrol_1_we4, or_1_out, or_2_out, unalignedbytestodword_1_p6;
  wire [7:0] B1_d1, B1_d2, B2_d1, B2_d2, B3_d1, B3_d2, B4_d1, B4_d2, dwordtounalignedbytes_1_b1,
       dwordtounalignedbytes_1_b2, dwordtounalignedbytes_1_b3, dwordtounalignedbytes_1_b4;
  wire [13:0] _1A_word__plus__1, _2A_word__plus__1, multiplexer_1_out, multiplexer_2_out, multiplexer_3_out,
       multiplexer_4_out, multiplexer_5_out, multiplexer_6_out;

  Add #(.Bits(14), .generic("this.Bits=int(args.addrBits-2);")) add_1 (
    .a(_1A[15:2]), .b(14'h1), .c_i(1'b0), .s(_1A_word__plus__1));  // open: c_o
  Add #(.Bits(14), .generic("this.Bits=int(args.addrBits-2);")) add_2 (
    .a(_2A[15:2]), .b(14'h1), .c_i(1'b0), .s(_2A_word__plus__1));  // open: c_o
  or or_1 (or_1_out, _1A[0], _1A[1]);
  or or_2 (or_2_out, _2A[0], _2A[1]);
  and and_1 (and_1_out, _1A[0], _1A[1]);
  and and_2 (and_2_out, _2A[0], _2A[1]);
  Multiplexer #(.Bits(14), .generic("this.AddrBits=int(args.addrBits-2);")) multiplexer_1 (
    .sel(or_1_out), .in_0(_1A[15:2]), .in_1(_1A_word__plus__1), .out(multiplexer_1_out));
  Multiplexer #(.Bits(14), .generic("this.AddrBits=int(args.addrBits-2);")) multiplexer_2 (
    .sel(or_2_out), .in_0(_2A[15:2]), .in_1(_2A_word__plus__1), .out(multiplexer_2_out));
  Multiplexer #(.Bits(14), .generic("this.AddrBits=int(args.addrBits-2);")) multiplexer_3 (
    .sel(_1A[1]), .in_0(_1A[15:2]), .in_1(_1A_word__plus__1), .out(multiplexer_3_out));
  Multiplexer #(.Bits(14), .generic("this.AddrBits=int(args.addrBits-2);")) multiplexer_4 (
    .sel(_2A[1]), .in_0(_2A[15:2]), .in_1(_2A_word__plus__1), .out(multiplexer_4_out));
  Multiplexer #(.Bits(14), .generic("this.AddrBits=int(args.addrBits-2);")) multiplexer_5 (
    .sel(and_1_out), .in_0(_1A[15:2]), .in_1(_1A_word__plus__1), .out(multiplexer_5_out));
  Multiplexer #(.Bits(14), .generic("this.AddrBits=int(args.addrBits-2);")) multiplexer_6 (
    .sel(and_2_out), .in_0(_2A[15:2]), .in_1(_2A_word__plus__1), .out(multiplexer_6_out));
  dwordToUnalignedBytes dwordtounalignedbytes_1 (
    .off(_1A[1:0]), .D(_1Din), .b4(dwordtounalignedbytes_1_b4), .b3(dwordtounalignedbytes_1_b3),
    .b2(dwordtounalignedbytes_1_b2), .b1(dwordtounalignedbytes_1_b1));
  memoryWriteControl memorywritecontrol_1 (
    .off(_1A[1:0]), .we(we), .am(am), .we4(memorywritecontrol_1_we4), .we3(memorywritecontrol_1_we3),
    .we2(memorywritecontrol_1_we2), .we1(memorywritecontrol_1_we1));
  RAMDualAccess #(.AddrBits(14), .Bits(8), .generic("this.AddrBits=int(args.addrBits-2);")) B4 (
    .str(memorywritecontrol_1_we4), .C(C), .ld(1'b1), .A1(multiplexer_1_out),
    .Din1(dwordtounalignedbytes_1_b4), .A2(multiplexer_2_out), .D1(B4_d1), .D2(B4_d2));
  RAMDualAccess #(.AddrBits(14), .Bits(8), .generic("this.AddrBits=int(args.addrBits-2);")) B3 (
    .str(memorywritecontrol_1_we3), .C(C), .ld(1'b1), .A1(multiplexer_3_out),
    .Din1(dwordtounalignedbytes_1_b3), .A2(multiplexer_4_out), .D1(B3_d1), .D2(B3_d2));
  RAMDualAccess #(.AddrBits(14), .Bits(8), .generic("this.AddrBits=int(args.addrBits-2);")) B2 (
    .str(memorywritecontrol_1_we2), .C(C), .ld(1'b1), .A1(multiplexer_5_out),
    .Din1(dwordtounalignedbytes_1_b2), .A2(multiplexer_6_out), .D1(B2_d1), .D2(B2_d2));
  RAMDualAccess #(.AddrBits(14), .Bits(8), .generic("this.AddrBits=int(args.addrBits-2);")) B1 (
    .str(memorywritecontrol_1_we1), .C(C), .ld(1'b1), .A1(_1A[15:2]), .Din1(dwordtounalignedbytes_1_b1),
    .A2(_2A[15:2]), .D1(B1_d1), .D2(B1_d2));
  // unalignedBytesToDword unalignedbytestodword_1: pin names not known; wires that end beside it: B4_d1, B3_d1, B2_d1, B1_d1, _1A[1:0], unalignedbytestodword_1_p6
  // unalignedBytesToDword unalignedbytestodword_2: pin names not known; wires that end beside it: B4_d2, B3_d2, B2_d2, B1_d2, _2A[1:0], _2D
  // memoryAccessTrimmer memoryaccesstrimmer_1: pin names not known; wires that end beside it: sign, am, unalignedbytestodword_1_p6, _1D

  // Other names for the same wires on the sheet: _1A_byte_offset[1:0] = _1A[1:0]; _1A_word[13:0] = _1A[15:2];
  //   _2A_byte_offset[1:0] = _2A[1:0]; _2A_word[13:0] = _2A[15:2]; clock = C

  // Notes on the sheet:
  //   C: Clock
  //   _1A: Address to be written or read from
  //   _2A: Address to be read from
  //   we: If the clock rises while this pin is high data is written
  //   am: Changes how may bytes is read or writen to 1A
  //   sign: Makes data read from 1A is sign extended
endmodule

/* Code that sets the parameters or builds the circuit:
addrBits := 16;
*/

/* Test case:
C  1A      1Din        2A     we am sign 1D          2D
0  0x0000  0x00000000  0x0000 0  0  0    0x00000000  0x00000000

# write dwords
C  0x0000  0x00000001  0x0000 1  0  0    0x00000001  0x00000001
C  0x0004  0xDEADBEEF  0x0000 1  0  0    0xDEADBEEF  0x00000001
C  0x0013  0xFED0DEAD  0x0000 1  0  0    0xFED0DEAD  0x00000001
C  0x0013  0x22222222  0x0000 0  0  0    0xFED0DEAD  0x00000001
C  0x4321  0xBEADFEED  0x0000 1  0  0    0xBEADFEED  0x00000001

# check dwords
C  0x0000  0x00000000  0x0000 0  0  0    0x00000001  0x00000001
C  0x0004  0x00000000  0x0000 0  0  0    0xDEADBEEF  0x00000001
C  0x0013  0x00000000  0x0000 0  0  0    0xFED0DEAD  0x00000001
C  0x4321  0x00000000  0x0013 0  0  0    0xBEADFEED  0xFED0DEAD
C  0x0000  0x00000000  0x4321 0  0  0    0x00000001  0xBEADFEED

# write words
C  0x0000  0xFEDCBA98  0x0000 1  2  0    0x0000BA98  0x0000BA98
C  0x0013  0x0000BEEF  0x0000 1  2  0    0x0000BEEF  0x0000BA98

# check words
C  0x0000  0x00000000  0x0000 0  0  0    0x0000BA98  0x0000BA98
C  0x0013  0x00000000  0x0013 0  0  0    0xFED0BEEF  0xFED0BEEF
C  0x0013  0x00000000  0x0013 0  2  0    0x0000BEEF  0xFED0BEEF
C  0x0013  0x00000000  0x0013 0  2  1    0xFFFFBEEF  0xFED0BEEF

# write byte
C  0x0004  0x01234567  0x0004 1  3  0    0x00000067  0xDEADBE67
C  0x0006  0x01234567  0x0006 1  3  0    0x00000067  0xBE670067

# check byte
C  0x0004  0x00000000  0x0004 0  0  0    0xDEADBE67  0xDEADBE67
C  0x0008  0x00000000  0x0008 0  0  0    0x00670000  0x00670000

# write triple
C  0xF001  0xABCDEF67  0xF001 1  1  0    0x00CDEF67  0x00CDEF67

# check triple
C  0xF001  0x00000000  0xF001 0  0  0    0x00CDEF67  0x00CDEF67
C  0xF001  0x00000000  0xF001 0  1  1    0xFFCDEF67  0x00CDEF67
*/
