// Digital circuit shiftLeft.dig as structural Verilog
module shiftLeft (
  input  [15:0] in,
  input  [15:0] fill,
  input  [3:0] shift,
  output [15:0] out,
  output [15:0] \cₒ 
);

  wire [15:0] \genericsplit16_1_msbₒ , genericsplit16_1_out, \genericsplit16_2_msbₒ , genericsplit16_2_out,
       \genericsplit16_3_msbₒ , genericsplit16_3_out, \genericsplit16_4_msbₒ , genericsplit16_4_out,
       \genericsplit16_5_msbₒ , genericsplit16_5_out, \genericsplit16_6_msbₒ , genericsplit16_6_out,
       \genericsplit16_7_msbₒ , genericsplit16_7_out, \genericsplit16_8_msbₒ , genericsplit16_8_out,
       \genericsplit16_9_msbₒ , genericsplit16_9_out, \genericsplit16_10_msbₒ , genericsplit16_10_out,
       \genericsplit16_11_msbₒ , genericsplit16_11_out, \genericsplit16_12_msbₒ , genericsplit16_12_out,
       \genericsplit16_13_msbₒ , genericsplit16_13_out, \genericsplit16_14_msbₒ , genericsplit16_14_out,
       \genericsplit16_15_msbₒ , genericsplit16_15_out;

  genericSplit16 #(.generic("split := 1;")) genericsplit16_1 (
    .\lsbᵢ (fill), .\msbᵢ (in), .out(genericsplit16_1_out), .\msbₒ (\genericsplit16_1_msbₒ ));  // open: lsbₒ
  genericSplit16 #(.generic("split := 2;")) genericsplit16_2 (
    .\lsbᵢ (fill), .\msbᵢ (in), .out(genericsplit16_2_out), .\msbₒ (\genericsplit16_2_msbₒ ));  // open: lsbₒ
  genericSplit16 #(.generic("split := 3;")) genericsplit16_3 (
    .\lsbᵢ (fill), .\msbᵢ (in), .out(genericsplit16_3_out), .\msbₒ (\genericsplit16_3_msbₒ ));  // open: lsbₒ
  genericSplit16 #(.generic("split := 4;")) genericsplit16_4 (
    .\lsbᵢ (fill), .\msbᵢ (in), .out(genericsplit16_4_out), .\msbₒ (\genericsplit16_4_msbₒ ));  // open: lsbₒ
  genericSplit16 #(.generic("split := 5;")) genericsplit16_5 (
    .\lsbᵢ (fill), .\msbᵢ (in), .out(genericsplit16_5_out), .\msbₒ (\genericsplit16_5_msbₒ ));  // open: lsbₒ
  genericSplit16 #(.generic("split := 6;")) genericsplit16_6 (
    .\lsbᵢ (fill), .\msbᵢ (in), .out(genericsplit16_6_out), .\msbₒ (\genericsplit16_6_msbₒ ));  // open: lsbₒ
  genericSplit16 #(.generic("split := 7;")) genericsplit16_7 (
    .\lsbᵢ (fill), .\msbᵢ (in), .out(genericsplit16_7_out), .\msbₒ (\genericsplit16_7_msbₒ ));  // open: lsbₒ
  genericSplit16 #(.generic("split := 8;")) genericsplit16_8 (
    .\lsbᵢ (fill), .\msbᵢ (in), .out(genericsplit16_8_out), .\msbₒ (\genericsplit16_8_msbₒ ));  // open: lsbₒ
  genericSplit16 #(.generic("split := 9;")) genericsplit16_9 (
    .\lsbᵢ (fill), .\msbᵢ (in), .out(genericsplit16_9_out), .\msbₒ (\genericsplit16_9_msbₒ ));  // open: lsbₒ
  genericSplit16 #(.generic("split := 10;")) genericsplit16_10 (
    .\lsbᵢ (fill), .\msbᵢ (in), .out(genericsplit16_10_out), .\msbₒ (\genericsplit16_10_msbₒ ));  // open: lsbₒ
  genericSplit16 #(.generic("split := 11;")) genericsplit16_11 (
    .\lsbᵢ (fill), .\msbᵢ (in), .out(genericsplit16_11_out), .\msbₒ (\genericsplit16_11_msbₒ ));  // open: lsbₒ
  genericSplit16 #(.generic("split := 12;")) genericsplit16_12 (
    .\lsbᵢ (fill), .\msbᵢ (in), .out(genericsplit16_12_out), .\msbₒ (\genericsplit16_12_msbₒ ));  // open: lsbₒ
  genericSplit16 #(.generic("split := 13;")) genericsplit16_13 (
    .\lsbᵢ (fill), .\msbᵢ (in), .out(genericsplit16_13_out), .\msbₒ (\genericsplit16_13_msbₒ ));  // open: lsbₒ
  genericSplit16 #(.generic("split := 14;")) genericsplit16_14 (
    .\lsbᵢ (fill), .\msbᵢ (in), .out(genericsplit16_14_out), .\msbₒ (\genericsplit16_14_msbₒ ));  // open: lsbₒ
  genericSplit16 #(.generic("split := 15;")) genericsplit16_15 (
    .\lsbᵢ (fill), .\msbᵢ (in), .out(genericsplit16_15_out), .\msbₒ (\genericsplit16_15_msbₒ ));  // open: lsbₒ
  Multiplexer #(.Selector_Bits(4), .Bits(16)) multiplexer_1 (
    .sel(shift), .in_0(in), .in_1(genericsplit16_1_out), .in_2(genericsplit16_2_out),
    .in_3(genericsplit16_3_out), .in_4(genericsplit16_4_out), .in_5(genericsplit16_5_out),
    .in_6(genericsplit16_6_out), .in_7(genericsplit16_7_out), .in_8(genericsplit16_8_out),
    .in_9(genericsplit16_9_out), .in_10(genericsplit16_10_out), .in_11(genericsplit16_11_out),
    .in_12(genericsplit16_12_out), .in_13(genericsplit16_13_out), .in_14(genericsplit16_14_out),
    .in_15(genericsplit16_15_out), .out(out));
  Multiplexer #(.Selector_Bits(4), .Bits(16)) multiplexer_2 (
    .sel(shift), .in_0({16{1'b0}}), .in_1(\genericsplit16_1_msbₒ ), .in_2(\genericsplit16_2_msbₒ ),
    .in_3(\genericsplit16_3_msbₒ ), .in_4(\genericsplit16_4_msbₒ ), .in_5(\genericsplit16_5_msbₒ ),
    .in_6(\genericsplit16_6_msbₒ ), .in_7(\genericsplit16_7_msbₒ ), .in_8(\genericsplit16_8_msbₒ ),
    .in_9(\genericsplit16_9_msbₒ ), .in_10(\genericsplit16_10_msbₒ ), .in_11(\genericsplit16_11_msbₒ ),
    .in_12(\genericsplit16_12_msbₒ ), .in_13(\genericsplit16_13_msbₒ ), .in_14(\genericsplit16_14_msbₒ ),
    .in_15(\genericsplit16_15_msbₒ ), .out(\cₒ ));

  // Other names for the same wires on the sheet: split[3:0] = shift
endmodule

/* Test case:
in	fill	shift	out	cₒ
0x844B	0xD221	0x0	0x844B	0x0000
0x844B	0xD221	0x1	0x0897	0x0001
0x844B	0xD221	0x2	0x112F	0x0002
0x844B	0xD221	0x3	0x225E	0x0004
0x844B	0xD221	0x4	0x44BD	0x0008
0x844B	0xD221	0x5	0x897A	0x0010
0x844B	0xD221	0x6	0x12F4	0x0021
0x844B	0xD221	0x7	0x25E9	0x0042
0x844B	0xD221	0x8	0x4BD2	0x0084
0x844B	0xD221	0x9	0x97A4	0x0108
0x844B	0xD221	0xa	0x2F48	0x0211
0x844B	0xD221	0xb	0x5E91	0x0422
0x844B	0xD221	0xc	0xBD22	0x0844
0x844B	0xD221	0xd	0x7A44	0x1089
0x844B	0xD221	0xe	0xF488	0x2112
0x844B	0xD221	0xf	0xE910	0x4225
*/
