// Digital circuit shiftRight.dig as structural Verilog
module shiftRight (
  input  [15:0] in,
  input  [15:0] fill,
  input  [3:0] shift,
  output [15:0] out,
  output [15:0] \cₒ 
);

  wire [15:0] \genericsplit16_1_lsbₒ , genericsplit16_1_out, \genericsplit16_2_lsbₒ , genericsplit16_2_out,
       \genericsplit16_3_lsbₒ , genericsplit16_3_out, \genericsplit16_4_lsbₒ , genericsplit16_4_out,
       \genericsplit16_5_lsbₒ , genericsplit16_5_out, \genericsplit16_6_lsbₒ , genericsplit16_6_out,
       \genericsplit16_7_lsbₒ , genericsplit16_7_out, \genericsplit16_8_lsbₒ , genericsplit16_8_out,
       \genericsplit16_9_lsbₒ , genericsplit16_9_out, \genericsplit16_10_lsbₒ , genericsplit16_10_out,
       \genericsplit16_11_lsbₒ , genericsplit16_11_out, \genericsplit16_12_lsbₒ , genericsplit16_12_out,
       \genericsplit16_13_lsbₒ , genericsplit16_13_out, \genericsplit16_14_lsbₒ , genericsplit16_14_out,
       \genericsplit16_15_lsbₒ , genericsplit16_15_out;

  genericSplit16 #(.generic("split := 15;")) genericsplit16_1 (
    .\lsbᵢ (in), .\msbᵢ (fill), .out(genericsplit16_1_out), .\lsbₒ (\genericsplit16_1_lsbₒ ));  // open: msbₒ
  genericSplit16 #(.generic("split := 14;")) genericsplit16_2 (
    .\lsbᵢ (in), .\msbᵢ (fill), .out(genericsplit16_2_out), .\lsbₒ (\genericsplit16_2_lsbₒ ));  // open: msbₒ
  genericSplit16 #(.generic("split := 13;")) genericsplit16_3 (
    .\lsbᵢ (in), .\msbᵢ (fill), .out(genericsplit16_3_out), .\lsbₒ (\genericsplit16_3_lsbₒ ));  // open: msbₒ
  genericSplit16 #(.generic("split := 12;")) genericsplit16_4 (
    .\lsbᵢ (in), .\msbᵢ (fill), .out(genericsplit16_4_out), .\lsbₒ (\genericsplit16_4_lsbₒ ));  // open: msbₒ
  genericSplit16 #(.generic("split := 11;")) genericsplit16_5 (
    .\lsbᵢ (in), .\msbᵢ (fill), .out(genericsplit16_5_out), .\lsbₒ (\genericsplit16_5_lsbₒ ));  // open: msbₒ
  genericSplit16 #(.generic("split := 10;")) genericsplit16_6 (
    .\lsbᵢ (in), .\msbᵢ (fill), .out(genericsplit16_6_out), .\lsbₒ (\genericsplit16_6_lsbₒ ));  // open: msbₒ
  genericSplit16 #(.generic("split := 9;")) genericsplit16_7 (
    .\lsbᵢ (in), .\msbᵢ (fill), .out(genericsplit16_7_out), .\lsbₒ (\genericsplit16_7_lsbₒ ));  // open: msbₒ
  genericSplit16 #(.generic("split := 8;")) genericsplit16_8 (
    .\lsbᵢ (in), .\msbᵢ (fill), .out(genericsplit16_8_out), .\lsbₒ (\genericsplit16_8_lsbₒ ));  // open: msbₒ
  genericSplit16 #(.generic("split := 7;")) genericsplit16_9 (
    .\lsbᵢ (in), .\msbᵢ (fill), .out(genericsplit16_9_out), .\lsbₒ (\genericsplit16_9_lsbₒ ));  // open: msbₒ
  genericSplit16 #(.generic("split := 6;")) genericsplit16_10 (
    .\lsbᵢ (in), .\msbᵢ (fill), .out(genericsplit16_10_out), .\lsbₒ (\genericsplit16_10_lsbₒ ));  // open: msbₒ
  genericSplit16 #(.generic("split := 5;")) genericsplit16_11 (
    .\lsbᵢ (in), .\msbᵢ (fill), .out(genericsplit16_11_out), .\lsbₒ (\genericsplit16_11_lsbₒ ));  // open: msbₒ
  genericSplit16 #(.generic("split := 4;")) genericsplit16_12 (
    .\lsbᵢ (in), .\msbᵢ (fill), .out(genericsplit16_12_out), .\lsbₒ (\genericsplit16_12_lsbₒ ));  // open: msbₒ
  genericSplit16 #(.generic("split := 3;")) genericsplit16_13 (
    .\lsbᵢ (in), .\msbᵢ (fill), .out(genericsplit16_13_out), .\lsbₒ (\genericsplit16_13_lsbₒ ));  // open: msbₒ
  genericSplit16 #(.generic("split := 2;")) genericsplit16_14 (
    .\lsbᵢ (in), .\msbᵢ (fill), .out(genericsplit16_14_out), .\lsbₒ (\genericsplit16_14_lsbₒ ));  // open: msbₒ
  genericSplit16 #(.generic("split := 1;")) genericsplit16_15 (
    .\lsbᵢ (in), .\msbᵢ (fill), .out(genericsplit16_15_out), .\lsbₒ (\genericsplit16_15_lsbₒ ));  // open: msbₒ
  Multiplexer #(.Selector_Bits(4), .Bits(16)) multiplexer_1 (
    .sel(shift), .in_0(in), .in_1(genericsplit16_1_out), .in_2(genericsplit16_2_out),
    .in_3(genericsplit16_3_out), .in_4(genericsplit16_4_out), .in_5(genericsplit16_5_out),
    .in_6(genericsplit16_6_out), .in_7(genericsplit16_7_out), .in_8(genericsplit16_8_out),
    .in_9(genericsplit16_9_out), .in_10(genericsplit16_10_out), .in_11(genericsplit16_11_out),
    .in_12(genericsplit16_12_out), .in_13(genericsplit16_13_out), .in_14(genericsplit16_14_out),
    .in_15(genericsplit16_15_out), .out(out));
  Multiplexer #(.Selector_Bits(4), .Bits(16)) multiplexer_2 (
    .sel(shift), .in_0({16{1'b0}}), .in_1(\genericsplit16_1_lsbₒ ), .in_2(\genericsplit16_2_lsbₒ ),
    .in_3(\genericsplit16_3_lsbₒ ), .in_4(\genericsplit16_4_lsbₒ ), .in_5(\genericsplit16_5_lsbₒ ),
    .in_6(\genericsplit16_6_lsbₒ ), .in_7(\genericsplit16_7_lsbₒ ), .in_8(\genericsplit16_8_lsbₒ ),
    .in_9(\genericsplit16_9_lsbₒ ), .in_10(\genericsplit16_10_lsbₒ ), .in_11(\genericsplit16_11_lsbₒ ),
    .in_12(\genericsplit16_12_lsbₒ ), .in_13(\genericsplit16_13_lsbₒ ), .in_14(\genericsplit16_14_lsbₒ ),
    .in_15(\genericsplit16_15_lsbₒ ), .out(\cₒ ));

  // Other names for the same wires on the sheet: split[3:0] = shift
endmodule

/* Test case:
in	fill	shift	out	cₒ
0x844B	0xD221	0x0	0x844B	0x0000
0x844B	0xD221	0x1	0xC225	0x8000
0x844B	0xD221	0x2	0x6112	0xC000
0x844B	0xD221	0x3	0x3089	0x6000
0x844B	0xD221	0x4	0x1844	0xB000
0x844B	0xD221	0x5	0x0C22	0x5800
0x844B	0xD221	0x6	0x8611	0x2C00
0x844B	0xD221	0x7	0x4308	0x9600
0x844B	0xD221	0x8	0x2184	0x4B00
0x844B	0xD221	0x9	0x10C2	0x2580
0x844B	0xD221	0xa	0x8861	0x12C0
0x844B	0xD221	0xb	0x4430	0x8960
0x844B	0xD221	0xc	0x2218	0x44B0
0x844B	0xD221	0xd	0x910C	0x2258
0x844B	0xD221	0xe	0x4886	0x112C
0x844B	0xD221	0xf	0xA443	0x896
*/
