// Digital circuit unalignedBytesToDword.dig as structural Verilog
module unalignedBytesToDword (
  input  [7:0] b4,
  input  [7:0] b3,
  input  [7:0] b2,
  input  [7:0] b1,
  input  [15:0] off,
  output [31:0] wd
);

  Multiplexer #(.Selector_Bits(2), .Bits(32)) multiplexer_1 (
    .sel(off[1:0]), .in_0({b4, b3, b2, b1}), .in_1({b3, b2, b1, b4}), .in_2({b2, b1, b4, b3}),
    .in_3({b1, b4, b3, b2}), .out(wd));
  // Pins of 2 and 16 bits meet at off
  // Pins of 1 and 32 bits meet at wd
endmodule
